# Fritzing sketch 01_led_yakma (saved by Fritzing 0.9.2b)
breadboards: 1

parts:
  Eleman1 = Arduino Uno (Rev3)
  R1 = Resistor [tolerance=±5% resistance=330 package=THT]
  LED1 = LED - 5mm [color="Red (633nm)" package="5 mm [THT]"]

nets:
  N1: Eleman1.D8, LED1.anode
  N2: Eleman1.GND, R1.Pin_0
  N3: R1.Pin_1, LED1.cathode
