# Fritzing sketch 03_analog_deger_okuma (saved by Fritzing 0.9.2b)
breadboards: 1

parts:
  Eleman1 = Arduino Uno (Rev3)
  R1 = Rotary Potentiometer (Small) [maximum_resistance=100kΩ package=THT]

nets:
  N1: Eleman1.A0, R1.wiper
  N2: Eleman1.5V, R1.leg1
  N3: Eleman1.GND, R1.leg2
