# Fritzing sketch 04_potansiyometre_ile_led_yakma (saved by Fritzing 0.9.2b)
breadboards: 1

parts:
  Eleman2 = Arduino Uno (Rev3)
  R2 = Rotary Potentiometer (Small) [maximum_resistance=100kΩ package=THT]
  R3 = Resistor [tolerance=±5% resistance=330 package=THT]
  LED1 = LED - 5mm [color="Red (633nm)" package="5 mm [THT]"]

nets:
  N1: Eleman2.A0, R2.wiper
  N2: Eleman2.GND, R2.leg2, R3.Pin_0
  N3: Eleman2.D3_PWM, LED1.anode
  N4: Eleman2.5V, R2.leg1
  N5: R3.Pin_1, LED1.cathode
