# Fritzing sketch 05_karasimsek (saved by Fritzing 0.9.2b)
breadboards: 1

parts:
  Eleman1 = Arduino Uno (Rev3)
  LED2 = LED - 5mm [color="Red (633nm)" package="5 mm [THT]"]
  LED3 = LED - 5mm [color="Red (633nm)" package="5 mm [THT]"]
  LED4 = LED - 5mm [color="Red (633nm)" package="5 mm [THT]"]
  LED5 = LED - 5mm [color="Red (633nm)" package="5 mm [THT]"]
  LED6 = LED - 5mm [color="Yellow (595nm)" package="5 mm [THT]"]
  LED1 = smd LED [color="Yellow (595nm)" package="0603 [SMD]"]
  R1 = Resistor [tolerance=±5% resistance=330 package=THT]
  R2 = Resistor [tolerance=±5% resistance=330 package=THT]
  R3 = Resistor [tolerance=±5% resistance=330 package=THT]
  R4 = Resistor [tolerance=±5% resistance=330 package=THT]
  R5 = Resistor [tolerance=±5% resistance=330 package=THT]
  R6 = Resistor [tolerance=±5% resistance=330 package=THT]

nets:
  N1: Eleman1.GND, LED2.cathode, LED3.cathode, LED4.cathode, LED5.cathode, LED6.cathode, LED1.cathode
  N2: Eleman1.D2, R1.Pin_1
  N3: Eleman1.D3_PWM, R4.Pin_1
  N4: Eleman1.D4, R5.Pin_1
  N5: Eleman1.D5_PWM, R3.Pin_1
  N6: Eleman1.D6_PWM, R6.Pin_1
  N7: Eleman1.D7, R2.Pin_1
  N8: LED2.anode, R1.Pin_0
  N9: LED3.anode, R5.Pin_0
  N10: LED4.anode, R3.Pin_0
  N11: LED5.anode, R6.Pin_0
  N12: LED6.anode, R2.Pin_0
  N13: LED1.anode, R4.Pin_0
