# Fritzing sketch 06_ldr_ile_otomatik_lamba (saved by Fritzing 0.9.2b)
breadboards: 1

parts:
  Eleman1 = Arduino Uno (Rev3)
  R1 = Photocell (LDR) [package=THT]
  LED1 = LED - 5mm [color="Red (633nm)" package="5 mm [THT]"]
  R2 = Resistor [tolerance=±5% resistance=330 package=THT]
  R3 = Resistor [tolerance=±5% resistance=10k package=THT]

nets:
  N1: Eleman1.A0, R1.pin_1, R3.Pin_1
  N2: Eleman1.D3_PWM, R2.Pin_0
  N3: Eleman1.5V, R1.pin_0
  N4: Eleman1.GND, LED1.cathode, R3.Pin_0
  N5: LED1.anode, R2.Pin_1
