# Fritzing sketch 07_rgb_led (saved by Fritzing 0.9.2b)
breadboards: 1

parts:
  Eleman1 = Arduino Uno (Rev3)
  R1 = Rotary Potentiometer (Small) [maximum_resistance=100kΩ package=THT]
  R2 = Resistor [tolerance=±5% resistance=330 package=THT]
  R3 = Resistor [tolerance=±5% resistance=330 package=THT]
  R4 = Resistor [tolerance=±5% resistance=330 package=THT]
  LED1 = RGB LED - (4 legs) [package="5 mm [THT]"]  # not connected

nets:
  N1: Eleman1.A0, R1.wiper
  N2: Eleman1.D9_PWM, R4.Pin_1
  N3: Eleman1.D10_PWM/SS, R3.Pin_1
  N4: Eleman1.D11_PWM/MOSI, R2.Pin_0
  N5: Eleman1.5V, R1.leg1
  N6: Eleman1.GND, R1.leg2
