# Fritzing sketch 08_ntc_ile_sicaklik_olcumu (saved by Fritzing 0.9.2b)
breadboards: 1

parts:
  Eleman1 = Arduino Uno (Rev3)
  LED1 = LED - 5mm [color="Red (633nm)" package="5 mm [THT]"]
  R1 = Resistor [tolerance=±5% resistance=330 package=THT]
  R2 = Resistor [tolerance=±5% resistance=10 package=THT]
  R3 = Temperature Sensor (Thermistor) [thermistor_type=NTC package=THT]

nets:
  N1: Eleman1.A0, R2.Pin_1, R3.pin_0
  N2: Eleman1.D2, R1.Pin_1
  N3: Eleman1.5V, R3.pin_1
  N4: Eleman1.GND, LED1.cathode, R2.Pin_0
  N5: LED1.anode, R1.Pin_0
