# Fritzing sketch 09_lm35__ile_sicaklik_olcumu (saved by Fritzing 0.9.2b)
breadboards: 1

parts:
  Eleman1 = Arduino Uno (Rev3)
  T1 = LM35 Temperature Sensor [package="TO92 [THT]"]
  J1 = Piezo Speaker
  LED1 = LED - 5mm [color="Red (633nm)" package="5 mm [THT]"]
  R1 = Resistor [tolerance=±5% resistance=330 package=THT]
  R2 = Resistor [tolerance=±5% resistance=330 package=THT]

nets:
  N1: Eleman1.A0, T1.Vout
  N2: Eleman1.D8, R1.Pin_0
  N3: Eleman1.D9_PWM, R2.Pin_1
  N4: Eleman1.5V, T1.+Vs
  GND: Eleman1.GND, T1.GND, J1.pin1, LED1.cathode
  N5: J1.pin2, R1.Pin_1
  N6: LED1.anode, R2.Pin_0
