# Fritzing sketch 10_ultrosonik_ile_park_sensoru (saved by Fritzing 0.9.2b)
breadboards: 1

parts:
  Eleman1 = Arduino Uno (Rev3)
  J1 = Piezo Speaker
  Eleman2 = HC-SR04 Ultrasonic Rangemeter
  R2 = Resistor [tolerance=±5% resistance=10 package=THT]

nets:
  N1: Eleman1.D8, R2.Pin_1
  GND: Eleman1.GND, J1.pin1, Eleman2.GND
  N2: Eleman1.D6_PWM, Eleman2.Echo
  N3: Eleman1.D7, Eleman2.Trig
  5V: Eleman1.5V, Eleman2.VCC
  N4: J1.pin2, R2.Pin_0
