# Fritzing sketch 11_joystic_ile_servo_kontrolu (saved by Fritzing 0.9.2b)
breadboards: 1

parts:
  J1 = Basic Servo
  Eleman1 = Arduino Uno (Rev3)
  Mod1 = KY-023 Dual Axis Joystick Module [package="Breakout board"]

nets:
  GND: J1.gnd, Eleman1.GND, Mod1.GND
  VCC: J1.vcc, Eleman1.5V, Mod1.+5V
  N1: J1.pulse, Eleman1.D3_PWM
  N2: Eleman1.A0, Mod1.VRx

custom parts:
  KY-023 Dual Axis Joystick Module: KY-023 Dual-Axis Joystick Module.
