# Fritzing sketch 12_dijital_metre_yapimi (saved by Fritzing 0.9.2b)
breadboards: 1

parts:
  Eleman1 = Arduino Uno (Rev3)
  LCD1 = LCD screen
  Eleman2 = HC-SR04 Ultrasonic Rangemeter
  R1 = Rotary Potentiometer (Small) [maximum_resistance=100kΩ package=THT]

nets:
  N1: Eleman1.D11_PWM/MOSI, LCD1.E
  N2: Eleman1.D12/MISO, LCD1.RS
  N3: Eleman1.D2, LCD1.DB7
  N4: Eleman1.D3_PWM, LCD1.DB6
  N5: Eleman1.D4, LCD1.DB5
  N6: Eleman1.D5_PWM, LCD1.DB4
  N7: Eleman1.D6_PWM, Eleman2.Echo
  N8: Eleman1.D7, Eleman2.Trig
  5V: Eleman1.5V, LCD1.VDD, LCD1.LED+, Eleman2.VCC, R1.leg2
  GND: Eleman1.GND, LCD1.VSS, LCD1.R/W, LCD1.LED-, Eleman2.GND, R1.leg1
  N9: LCD1.V0, R1.wiper
