# Fritzing sketch 14_bluetooth_ile_rgb_led_kontrolu (saved by Fritzing 0.9.2b)
breadboards: 1

parts:
  Eleman1 = Arduino Uno (Rev3)
  Eleman2 = Bluetooth HC-06
  LED1 = RGB LED - (4 legs) [package="5 mm [THT]"]  # not connected

nets:
  N1: Eleman1.D0/RX, Eleman2.TXD
  N2: Eleman1.D1/TX, Eleman2.RXD
  5V: Eleman1.5V, Eleman2.VCC
  GND: Eleman1.GND, Eleman2.GND
