# Fritzing sketch 15_dijital_saat_yapimi (saved by Fritzing 0.9.2b)
breadboards: 1

parts:
  Eleman1 = Arduino Uno (Rev3)
  LCD1 = LCD screen
  R1 = Rotary Potentiometer (Small) [maximum_resistance=100kΩ package=THT]
  PCB2 = RTC_DS1302_module

nets:
  N1: Eleman1.D8, PCB2.RST
  N2: Eleman1.D11_PWM/MOSI, LCD1.E
  N3: Eleman1.D12/MISO, LCD1.RS
  N4: Eleman1.D2, LCD1.DB7
  N5: Eleman1.D3_PWM, LCD1.DB6
  N6: Eleman1.D4, LCD1.DB5
  N7: Eleman1.D5_PWM, LCD1.DB4
  N8: Eleman1.D6_PWM, PCB2.CLK
  N9: Eleman1.D7, PCB2.DAT
  5V: Eleman1.5V, LCD1.VDD, LCD1.LED+, R1.leg2, PCB2.VCC
  GND: Eleman1.GND, LCD1.VSS, LCD1.R/W, LCD1.LED-, R1.leg1, PCB2.GND
  N10: LCD1.V0, R1.wiper

custom parts:
  RTC_DS1302_module: Arduino module DS1302 SPI Real Time Clock
