# Fritzing sketch 16_rfid_ile_servo_kontrolu (saved by Fritzing 0.9.2b)
breadboards: 1

parts:
  Eleman2 = Arduino Uno (Rev3)
  J1 = Basic Servo
  Eleman1 = RFID-RC522 [part_number=101218]

nets:
  N1: Eleman2.D8, J1.pulse
  N2: Eleman2.D9_PWM, Eleman1.RST
  N3: Eleman2.D10_PWM/SS, Eleman1.SDA
  N4: Eleman2.D11_PWM/MOSI, Eleman1.MOSI
  N5: Eleman2.D12/MISO, Eleman1.MISO
  N6: Eleman2.D13/SCK, Eleman1.SCK
  5V: Eleman2.5V, J1.vcc, Eleman1.3.3V
  GND: Eleman2.GND, J1.gnd, Eleman1.GND
