# Fritzing sketch 17_esp8266_ile_sicaklik_ve_nem_olcumu (saved by Fritzing 0.9.2b)
breadboards: 1

parts:
  Eleman1 = Arduino Uno (Rev3)
  U1 = ESP8266 WiFi Module [part_number=ESP8266]
  DHT11_1 = DHT11 module

nets:
  GND: Eleman1.D10_PWM/SS, Eleman1.GND, U1.GND, U1.TXD, DHT11_1.GND
  3V3: Eleman1.D11_PWM/MOSI, Eleman1.3V3, U1.RXD, U1.VCC, U1.GPIO_2, U1.CH_PD
  N1: Eleman1.D2, DHT11_1.DATA
  5V: Eleman1.5V, DHT11_1.VCC
  N2: U1.GPIO_0, U1.RST

custom parts:
  ESP8266 WiFi Module: Generic WiFi Module based on the ESP8266 with onboard PCB antenna and UART communications
  DHT11 module: DHT11 black pcb module
